# Fritzing sketch Board (saved by Fritzing 0.9.3b)
circuit board: 8.04827cm x 2.65986cm
breadboards: 1

parts:
  Arduino_Nano = Arduino Nano (Rev3.0)
  Jack_6_35 = AMPHENOL - ACJS-MHDR [package=ACJS-MHDR]

nets (from the schematic view):
  GND: Arduino_Nano.GND, Jack_6_35.Sleeve_(1)
  5V: Arduino_Nano.VIN
  N1: Arduino_Nano.A0, Jack_6_35.Ring_(2)
  N2: Arduino_Nano.AREF, Arduino_Nano.3V3, Jack_6_35.Tip_(3)
