# Fritzing sketch MAUDIO EX-P (saved by Fritzing 0.9.3b)
circuit board: 8.46667cm x 5.64444cm
breadboards: 1

parts:
  Jack_IN = 2.5mm Audio Jack [package=stereojack2.5mm_smd]
  Polarity_switch = SPDT Slide Switch [package=ayz0202]
  B12K77 = Rotary Potentiometer (Small) [part_number=Pedal package=THT]
  R2 = Resistor [tolerance=±5% resistance=1k package=THT]
  R3 = Rotary Potentiometer (Small) [maximum_resistance=100kΩ part_number=Sensitivity package=THT]

nets:
  N1: Jack_IN.LEFT, Polarity_switch.2
  N2: Jack_IN.RIGHT, Polarity_switch.3
  N3: Jack_IN.SLEEVE, R3.wiper, R3.leg2
  N4: Polarity_switch.1, Polarity_switch.6
  N5: Polarity_switch.5, B12K77.leg2
  N6: Polarity_switch.4, R2.Pin_1
  N7: B12K77.leg1, R3.leg1
  N8: B12K77.wiper, R2.Pin_0
