# Fritzing sketch USB-MIDI (saved by Fritzing 0.9.3b)
breadboards: 1

parts:
  B12K77 = Rotary Potentiometer (Small) [part_number=Pedal package=THT]
  R3 = Rotary Potentiometer (Small) [maximum_resistance=100kΩ part_number=Sensitivity package=THT]
  Arduino_Pro_Mini = Arduino Pro Mini v13

nets:
  N1: B12K77.leg1, R3.leg1, Arduino_Pro_Mini.GND
  N2: B12K77.wiper, R3.leg2
  N3: B12K77.leg2, Arduino_Pro_Mini.VCC
  N4: R3.wiper, Arduino_Pro_Mini.A0
